// Logisim project 1bit_summator.circ as structural Verilog: 1 circuit, main circuit main
module main (
  input  a,
  input  b,
  input  c,
  output P,
  output nP,
  output P_,
  output S
);

  wire and_1_out, and_2_out, and_3_out, and_4_out, not_1_out, not_2_out, not_3_out, or_1_out;

  not not_1 (not_1_out, a);
  not not_2 (not_2_out, b);
  not not_3 (not_3_out, c);
  and and_1 (and_1_out, a, not_2_out, c);
  and and_2 (and_2_out, a, not_3_out, b);
  and and_3 (and_3_out, b, c);
  or or_1 (or_1_out, a, b, c);
  and and_4 (and_4_out, a, b, c);
  or or_2 (P, and_1_out, and_2_out, and_3_out);
  not not_4 (nP, P);
  and and_5 (P_, nP, or_1_out);
  or or_3 (S, P_, and_4_out);

  // Notes on the sheet:
  //   b
  //   c
  //   a
  //   !a
  //   !b
  //   !c
  //   a&b&!c
  //   b&c
  //   a&!b&c
  //   a|b|c
  //   a&b&c
endmodule
