// Logisim project 1bit_summator2.circ as structural Verilog: 1 circuit, main circuit main
module main (
  input  a,
  input  b,
  input  c,
  output P,
  output S
);

  wire and_1_out, and_2_out, and_3_out, and_4_out, and_5_out, and_6_out, and_7_out, not_1_out, not_2_out,
       not_3_out;

  not not_1 (not_1_out, a);
  not not_2 (not_2_out, b);
  not not_3 (not_3_out, c);
  and and_1 (and_1_out, a, not_3_out, b);
  and and_2 (and_2_out, a, not_2_out, c);
  and and_3 (and_3_out, b, c);
  and and_4 (and_4_out, a, not_2_out, not_3_out);
  and and_5 (and_5_out, not_1_out, b, not_3_out);
  and and_6 (and_6_out, not_1_out, not_2_out, c);
  and and_7 (and_7_out, a, b, c);
  or or_1 (P, and_1_out, and_2_out, and_3_out);
  or or_2 (S, and_4_out, and_5_out, and_6_out, and_7_out);

  // Notes on the sheet:
  //   b
  //   a
  //   !a
  //   !b
  //   !c
  //   c
  //   !a
  //   !b
  //   !c
  //   a&b&!c
  //   a&!b&c
  //   b&c
  //   a&!b&!c
  //   !a&b&!c
  //   !a&!b&c
  //   a&b&c
endmodule
