// Logisim project trigger.circ as structural Verilog: 1 circuit, main circuit main
module main (
  input  V,
  output [2:0] out_2
);

  wire and_1_out, T1_qn, T2_qn;

  and and_1 (and_1_out, T1_qn, T2_qn);
  T_Flip_Flop T3 (.T(and_1_out), .clk(V), .Q(out_2[2]));  // open: Qn, reset, preset
  T_Flip_Flop T2 (.T(T1_qn), .clk(V), .Q(out_2[1]), .Qn(T2_qn));  // open: reset, preset
  T_Flip_Flop T1 (.T(V), .clk(V), .Q(out_2[0]), .Qn(T1_qn));  // open: reset, preset

  // Notes on the sheet:
  //   q2
  //   q1
  //   q3
  //   q2
  //   q1
endmodule
